# Fritzing sketch montaje_ventana (saved by Fritzing 0.9.4)
breadboards: 1

parts:
  Componente1 = Arduino Mega 2560 (Rev3)
  2_Channel_Relay1 = 2 Channel Power Relay
  YL-83_-_Control_Board1 = YL-83 Rain Sensor - Control Board
  VCC1 = Battery block 9V
  M1 = linear actuator [package=THT]
  VCC2 = 4 x AAA Battery Mount
  U1 = ESP8266 NodeMCU LoLin module
  J2 = Piezo Speaker
  J1 = Basic Servo
  YL-83_-_Detection_Board1 = YL-83 Rain Sensor - Detection Board

nets:
  N1: Componente1.D9_PWM, J1.pulse
  N2: Componente1.D8_PWM, J2.pin2
  GND: Componente1.GND, 2_Channel_Relay1.GND, YL-83_-_Control_Board1.GND, VCC2.-, U1.GND, J2.pin1, J1.gnd
  VIN: Componente1.VIN, 2_Channel_Relay1.VCC
  N3: Componente1.D31, U1.D0
  N4: Componente1.D33, U1.D1
  N5: Componente1.D35, U1.D2
  N6: Componente1.D37, U1.D3
  N7: Componente1.D39, U1.D5
  N8: Componente1.D41, U1.D6
  N9: Componente1.D43, U1.D7
  N10: Componente1.D52, 2_Channel_Relay1.IN2
  N11: Componente1.D53, 2_Channel_Relay1.IN1
  VCC: 2_Channel_Relay1.JD-VCC, YL-83_-_Control_Board1.VCC, VCC2.+, J1.vcc
  N12: 2_Channel_Relay1.K1-NC, 2_Channel_Relay1.K2-NC, VCC1.-
  N13: 2_Channel_Relay1.K1-COM, M1.pin2
  N14: 2_Channel_Relay1.K1-NO, 2_Channel_Relay1.K2-NO, VCC1.+
  N15: 2_Channel_Relay1.K2-COM, M1.pin1
  N16: YL-83_-_Control_Board1.AO, U1.A0
  N17: YL-83_-_Control_Board1.POS, YL-83_-_Detection_Board1.POS
  N18: YL-83_-_Control_Board1.NEG, YL-83_-_Detection_Board1.NEG

notes:
  D0 = A
  D1 = B
  D2 = C
  D3 = D
  D5 = E
  D6 = F
  D7 = G

custom parts:
  2 Channel Power Relay: A 2 channel power relay. The module operates at 5V.
  YL-83 Rain Sensor - Control Board: The YL-83 is a rain sensor that has more resistance when dry and less resistance when wet. The module runs at 5V.
  linear actuator: Generic linear actuator.
  ESP8266 NodeMCU LoLin module: ESP8266 based NodeMCU
  YL-83 Rain Sensor - Detection Board: The YL-83 is a rain sensor that has more resistance when dry and less resistance when wet. The module runs at 5V.
